# Fritzing sketch Controlled Motion System via Recognize Voice & Joystick (saved by Fritzing 0.9.4)
breadboards: 1

parts:
  Created_By_-_Refael_Ivgi_-_11_11_22 = Arduino Uno (Rev3)
  UltraSonic = HC-SR04 Ultrasonic Distance Sensor
  JoyStick = Black Joystick KY-023
  Recognize_Voice_Module = elechouse_voice_recognition_module_v3
  Controlled_Motion_System_via_Recognize_Voice_&_Joystick = Basic Servo

nets:
  N1: Created_By_-_Refael_Ivgi_-_11_11_22.A1, JoyStick.SW, JoyStick.VRy
  N2: Created_By_-_Refael_Ivgi_-_11_11_22.D10_PWM/SS, UltraSonic.TRIG
  N3: Created_By_-_Refael_Ivgi_-_11_11_22.D11_PWM/MOSI, UltraSonic.ECHO
  N4: Created_By_-_Refael_Ivgi_-_11_11_22.D0/RX, Recognize_Voice_Module.TXD
  N5: Created_By_-_Refael_Ivgi_-_11_11_22.D1/TX, Recognize_Voice_Module.RXD
  N6: Created_By_-_Refael_Ivgi_-_11_11_22.D7, Controlled_Motion_System_via_Recognize_Voice_&_Joystick.pulse
  3V3: Created_By_-_Refael_Ivgi_-_11_11_22.3V3, JoyStick.VRx, JoyStick.+5V
  VCC: Created_By_-_Refael_Ivgi_-_11_11_22.5V, UltraSonic.VCC, Recognize_Voice_Module.VCC, Controlled_Motion_System_via_Recognize_Voice_&_Joystick.vcc
  GND: Created_By_-_Refael_Ivgi_-_11_11_22.GND, UltraSonic.GND, JoyStick.GND, Controlled_Motion_System_via_Recognize_Voice_&_Joystick.gnd

custom parts:
  Black Joystick KY-023: Description: The joystick is a combination of 2 analoog potentiometer and a digital switch. Arduino GND --> Module pin - Arduino +5V --> Module pin +5V Arduino Analoog 0 --> Module VRx Arduino Analoog 1 --> Module VRy Arduino Digital --> Module SW Dimensions: 1" x 1.25"
  elechouse_voice_recognition_module_v3: Elechouse voice recognition module v3. Module that accepts up to 7 voice commands via a microphone. Note: currently this part was made from a .png image of the board. Thus the pcb is probably not correctly dimensioned since the input data was not precise. Before making boards based on this part, print out the footprint and check it (and provide corrections via the Fritzing forums to correct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
